# Fritzing sketch chickenguard_V2 (saved by Fritzing 0.9.3b)
circuit board: 8.46667cm x 5.64444cm

parts:
  Arduino_MEGA_2561 = Arduino Mega 2560 (Rev3)
  Switch_Bottom1 = Pushbutton [package=THT]
  Switch_Top1 = Pushbutton [package=THT]
  Scrolling_LCD = Pushbutton [package="[THT]"]
  Manual_Interrupt1 = Pushbutton [package="[THT]"]
  Close_Button1 = Pushbutton [package="[THT]"]
  Open_Button = Pushbutton [package="[THT]"]
  Automatic_Mode1 = Pushbutton [package="[THT]"]
  LCD1 = LCD screen
  LED_Door_Closed1 = LED - 5mm [color="Blue (430nm)" package="5 mm [THT]"]
  LED_Error1 = LED - 5mm [color="Red (633nm)" package="5 mm [THT]"]  # not connected
  IC2 = L293D [package=THT]
  Photoresistor1 = PHOTOCELL [package=photocell-kit]
  Motor1 = DC Motor
  DS3232 = Real Time Clock Module - DS1307 RTC Breakout Board
  Q2 = TRANSISTOR_NPN [package=to-92-ammo]
  R20 = Resistor [tolerance=±5% resistance=100k package=THT]
  R19 = Resistor [tolerance=±5% resistance=220 package=THT]
  R18 = Resistor [tolerance=±5% resistance=220 package=THT]
  R13 = Resistor [tolerance=±5% resistance=220 package=THT]
  R12 = Resistor [tolerance=±5% resistance=220 package=THT]
  R17 = Resistor [tolerance=±5% resistance=100 package=THT]
  R14 = Resistor [tolerance=±5% resistance=10k package=THT]
  Q3 = TRANSISTOR_NPN [package=to-92-ammo]
  R21 = Resistor [tolerance=±5% resistance=10k package=THT]
  R22 = Resistor [tolerance=±5% resistance=10k package=THT]
  Q4 = TRANSISTOR_NPN [package=to-92-ammo]
  LM1 = RioRand LM2596
  LM2 = RioRand LM2596
  Composant2 = Adafruit HUZZAH32 ESP32 Feather [part_number="Adafruit #3405"]
  J1 = Screw terminal - 2 pins [package=THT]  # not connected
  Composant3 = Logic Level Converter
  D2 = Rectifier Diode [part_number=1N4001 package="300 mil [THT]"]
  D3 = Rectifier Diode [part_number=1N4001 package="300 mil [THT]"]  # not connected
  R24 = Resistor [tolerance=±5% resistance=10k package=THT]
  Q6 = TRANSISTOR_NPN [package=to-92-ammo]
  Composant5 = Relay T73

nets:
  N1: Arduino_MEGA_2561.A2, Photoresistor1.P$2, R20.Pin_0
  N2: Arduino_MEGA_2561.D21/SCL, Arduino_MEGA_2561.SCL, DS3232.SCL
  N3: Arduino_MEGA_2561.D20/SDA, DS3232.SDA
  N4: Arduino_MEGA_2561.D8_PWM, Composant3.RX2_HV
  5V: Arduino_MEGA_2561.5V, DS3232.5V
  N5: Arduino_MEGA_2561.VIN, LM1.Pin_2
  N6: Arduino_MEGA_2561.D2_PWM, DS3232.SQW
  N7: Arduino_MEGA_2561.D3_PWM, Manual_Interrupt1.Pin_3, Manual_Interrupt1.Pin_4
  N8: Arduino_MEGA_2561.D5_PWM, IC2.Enable_1
  N9: Arduino_MEGA_2561.D22, R19.Pin_0
  N10: Arduino_MEGA_2561.D23, Open_Button.Pin_1, Open_Button.Pin_2
  N11: Arduino_MEGA_2561.D25, R18.Pin_0
  N12: Arduino_MEGA_2561.D26, Automatic_Mode1.Pin_1, Automatic_Mode1.Pin_2
  N13: Arduino_MEGA_2561.D28, Switch_Top1.leg0, R13.Pin_0
  N14: Arduino_MEGA_2561.D30, Close_Button1.Pin_1, Close_Button1.Pin_2
  N15: Arduino_MEGA_2561.D32, IC2.In_1
  N16: Arduino_MEGA_2561.D34, R24.Pin_0
  N17: Arduino_MEGA_2561.D35, IC2.In_2
  N18: Arduino_MEGA_2561.D36, R14.Pin_0
  N19: Arduino_MEGA_2561.D39, Scrolling_LCD.Pin_4
  N20: Arduino_MEGA_2561.D40, LCD1.DB7
  N21: Arduino_MEGA_2561.D42, LCD1.DB6
  N22: Arduino_MEGA_2561.D44, LCD1.DB5
  N23: Arduino_MEGA_2561.D46, LCD1.DB4
  N24: Arduino_MEGA_2561.D48, LCD1.E
  N25: Arduino_MEGA_2561.D50, LCD1.RS
  N26: Arduino_MEGA_2561.D52, R22.Pin_0
  N27: Arduino_MEGA_2561.D53, R21.Pin_0
  N28: Switch_Bottom1.leg0, R12.Pin_0
  N29: LCD1.VDD, Q4.C
  N30: LCD1.V0, Q3.C
  N31: LCD1.LED+, R17.Pin_0
  N32: LCD1.LED-, Q2.E
  N33: LED_Door_Closed1.cathode, R19.Pin_1
  N34: IC2.Out_1_(_Controlled_by_Enable_1_), Motor1.pin_2
  N35: IC2.Out_2_(_Controlled_by_Enable_1_), Motor1.pin_1
  N36: DS3232.GND, LM2.Pin_3
  N37: Q2.B, R14.Pin_1
  N38: Q3.B, R21.Pin_1
  N39: R22.Pin_1, Q4.B
  N40: LM1.Pin_0, LM2.Pin_0
  N41: LM1.Pin_1, LM2.Pin_1
  N42: LM2.Pin_2, D2.anode
  N43: Composant2.IO17, Composant3.RX2_LV
  N44: Composant2.3.3V, Composant3.LV
  N45: Composant2.VBAT, Composant5.NC
  N46: D2.cathode, Composant5.COM
  N47: R24.Pin_1, Q6.B
  N48: Q6.C, Composant5.C1

notes:
  Automatic Mode
  Switch Bottom
  Close button
  Door is closed
  LCD Scrolling
  Switch Top
  Photo Resistor
  Back Light
  Wake Up Manual
  Blink Error
  220 Ohms
  100 Ohms
  10 KOhms
  5 Volts
  100 KOhms
  Light Contrast
  Motor
  Open Button
  DS3231
  LCD
  ChickenGuard Version 2
  C
  E
  9 Volts
  VBatt 12-14 Volts
  Logic Level Shifter
  Geekcreit ESP 32
  Converter DC/DC LM2596
  3,3 Volts
  vincent.huynen@gmail.com - 2019
  Diode
  Relay

custom parts:
  Relay T73: An T73 Mini PCB Relay
